# Fritzing sketch board (saved by Fritzing 0.9.3b)
breadboards: 2

parts:
  Stop_Button = Pushbutton [package="[THT]"]
  Start_Button = Pushbutton [package="[SMD]"]
  Part1 = Arduino Nano (Rev3.0) (ICSP)
  Squix1 = OLED 0.96" 128x64 I2C SSD1306
  Q1 = Basic FET N-Channel [package="TO220 [THT]"]
  R1 = Resistor [tolerance=±0.5% resistance=100 package=THT]
  R2 = Resistor [tolerance=±5% resistance=100 package=THT]
  R3 = Resistor [tolerance=±5% resistance=100 package=THT]
  +12v = Screw terminal - 2 pins [package=THT]
  R4 = Resistor [tolerance=±5% resistance=100 package=THT]
  Mode_Select = Toggle Switch [package=THT]
  Time_LED_2 = LED - 3mm [color="Red (633nm)" package="3 mm [THT]"]
  Time_LED_0 = LED - 3mm [color="Red (633nm)" package="3 mm [THT]"]
  Time_LED_1 = LED - 3mm [color="Red (633nm)" package="3 mm [THT]"]
  Pololu_A1 = Pololu A4988 [package=SO16]
  R5 = Resistor [tolerance=±5% resistance=560 package=THT]
  R6 = Resistor [tolerance=±5% resistance=560 package=THT]
  R7 = Resistor [tolerance=±5% resistance=560 package=THT]
  Time_Select_0 = Pushbutton [package="[THT]"]
  R8 = Resistor [tolerance=±5% resistance=100 package=THT]
  M1 = Stepper Motor - Bipolar
  C1 = Electrolytic Capacitor [capacitance=100nF voltage=20V package="100 mil [THT, electrolytic]"]
  Cure_Mode_LED = LED - 3mm [color="Red (633nm)" package="3 mm [THT]"]
  Wash_Mode_LED = LED - 3mm [color="Red (633nm)" package="3 mm [THT]"]
  R9 = Resistor [tolerance=±5% resistance=560 package=THT]
  R10 = Resistor [tolerance=±5% resistance=560 package=THT]
  J2 = Piezo Speaker
  Time_Select_1 = Pushbutton [package="[THT]"]
  R11 = Resistor [tolerance=±5% resistance=100 package=THT]
  Time_Select_2 = Pushbutton [package="[THT]"]
  R12 = Resistor [tolerance=±5% resistance=100 package=THT]
  safety_override = Reed switch [package=THT]
  safety_switch = Reed switch [package=THT]
  R13 = Resistor [tolerance=±5% resistance=100 package=THT]
  R14 = Resistor [tolerance=±5% resistance=100 package=THT]
  LED1 = LED - 3mm [color="Red (633nm)" package="3 mm [THT]"]

nets:
  N1: Stop_Button.Pin_1, Stop_Button.Pin_2, Part1.D11/MOSI, R3.Pin_1
  5V: Stop_Button.Pin_3, Stop_Button.Pin_4, Start_Button.Pin_3, Start_Button.Pin_4, Part1.5V, Squix1.VCC, Mode_Select.COM, Pololu_A1.VDD, Time_Select_0.Pin_3, Time_Select_0.Pin_4, Time_Select_1.Pin_3, Time_Select_1.Pin_4, safety_override.pin_2, safety_switch.pin_2
  N2: Start_Button.Pin_1, Start_Button.Pin_2, Part1.D13/SCK, R4.Pin_1
  GND: Part1.GND, Squix1.GND, Q1.source, R1.Pin_0, R2.Pin_0, R3.Pin_0, +12v.pin1, R4.Pin_0, Time_LED_2.cathode, Time_LED_0.cathode, Time_LED_1.cathode, Pololu_A1.GND, R8.Pin_0, C1.-, Cure_Mode_LED.cathode, Wash_Mode_LED.cathode, J2.pin1, R12.Pin_0, R13.Pin_1, R14.Pin_1
  N3: Part1.D2, Pololu_A1.DIR
  N4: Part1.D3, Pololu_A1.STEP
  N5: Part1.D4, R9.Pin_1
  N6: Part1.D5, Pololu_A1.MS1, Pololu_A1.MS2, Pololu_A1.MS3, R10.Pin_1
  N7: Part1.D6, Time_Select_0.Pin_1, Time_Select_0.Pin_2, R8.Pin_1
  N8: Part1.D7, Time_Select_1.Pin_1, Time_Select_1.Pin_2, R11.Pin_1
  N9: Part1.D8, Time_Select_2.Pin_1, Time_Select_2.Pin_2, R12.Pin_1
  N10: Part1.D9, Q1.gate, R1.Pin_1
  N11: Part1.D10, R2.Pin_1, Mode_Select.L2
  N12: Part1.D12/MISO, J2.pin2
  N13: Part1.VIN, +12v.pin2, Pololu_A1.VMOT, C1.+, LED1.anode
  N14: Part1.A7, safety_override.pin_1, R14.Pin_0
  N15: Part1.A6, safety_switch.pin_1, R13.Pin_0
  N16: Part1.A5, Squix1.SCL
  N17: Part1.A4, Squix1.SCA
  N18: Part1.A3, Pololu_A1.ENABLE
  N19: Part1.A2, R6.Pin_1
  N20: Part1.A1, R7.Pin_1
  N21: Part1.A0, R5.Pin_1
  N22: Q1.drain, LED1.cathode
  N23: Time_LED_2.anode, R6.Pin_0
  N24: Time_LED_0.anode, R5.Pin_0
  N25: Time_LED_1.anode, R7.Pin_0
  N26: Pololu_A1.RESET, Pololu_A1.SLEEP
  N27: Pololu_A1.1B, M1.A
  N28: Pololu_A1.1A, M1.C
  N29: Pololu_A1.2A, M1.B
  N30: Pololu_A1.2B, M1.D
  N31: Cure_Mode_LED.anode, R10.Pin_0
  N32: Wash_Mode_LED.anode, R9.Pin_0
  N33: Time_Select_2.Pin_3, Time_Select_2.Pin_4
